// Logisim project ALU.circ as structural Verilog: 5 circuits, main circuit main
module main (
);

  mux2 mux2_1 ();  // open: A, B, in_3, out_4
endmodule

module mux2 (
  input  A,
  input  B,
  input  in_3,
  output out_4
);

  wire and_1_out, and_2_out, not_1_out;

  not not_1 (not_1_out, in_3);
  and and_1 (and_1_out, A, not_1_out);
  and and_2 (and_2_out, B, in_3);
  or or_1 (out_4, and_1_out, and_2_out);
endmodule

module mux4 (
  input  in_1,
  input  in_2,
  input  in_3,
  input  in_4,
  input  in_5,
  input  in_6,
  output out_7
);

  wire mux2_1_out_4, mux2_2_out_4;

  mux2 mux2_1 (.A(in_1), .B(in_2), .in_3(in_5), .out_4(mux2_1_out_4));
  mux2 mux2_2 (.A(in_3), .B(in_4), .in_3(in_5), .out_4(mux2_2_out_4));
  mux2 mux2_3 (.A(mux2_1_out_4), .B(mux2_2_out_4), .in_3(in_6), .out_4(out_7));
endmodule

module mux8 (
  input  in_1,
  input  in_2,
  input  in_3,
  input  in_4,
  input  in_5,
  input  in_6,
  input  in_7,
  input  in_8,
  input  in_9,
  input  in_10,
  input  in_11,
  output out_12
);

  wire mux4_1_out_7, mux4_2_out_7;

  mux4 mux4_1 (.in_1(in_1), .in_2(in_2), .in_3(in_3), .in_4(in_4), .in_5(in_9), .in_6(in_10), .out_7(mux4_1_out_7));
  mux4 mux4_2 (.in_1(in_5), .in_2(in_6), .in_3(in_7), .in_4(in_8), .in_5(in_9), .in_6(in_10), .out_7(mux4_2_out_7));
  mux2 mux2_1 (.A(mux4_1_out_7), .B(mux4_2_out_7), .in_3(in_11), .out_4(out_12));
endmodule

module mux_64_a_8 (
);

  mux8 mux8_1 ();  // open: in_1, in_2, in_3, in_4, in_5, in_6, in_7, in_8, in_9, in_10, in_11, out_12
endmodule
